# Fritzing sketch project schematic (saved by Fritzing 0.9.3b)
breadboards: 1

parts:
  NoduMcu = ESP8266 WiFi Module [part_number=ESP8266]
  Arduino = Arduino Uno (Rev3) - ICSP
  Light_sensor = Photocell (LDR) [package=THT]
  Tempreture_sensor = LM35 Temperature Sensor [package="TO92 [THT]"]
  alarm_buzzer = Buzzer 12mm [package=buzzer-ccv-kit]
  R2 = Resistor [tolerance=±10% resistance=100k package=THT]
  MQ2_Gas_Sensor = GAS_SENSOR [package=mq-3]

nets:
  N1: NoduMcu.GPIO_14, Arduino.D10_PWM/SS
  N2: NoduMcu.GPIO_12, Arduino.D9_PWM
  N3: NoduMcu.GPIO_13, Arduino.ICSP_MOSI, Arduino.D11_PWM/MOSI
  N4: Arduino.A0, Tempreture_sensor.Vout
  N5: Arduino.A1, Light_sensor.pin_1, R2.Pin_0
  N6: Arduino.A3, MQ2_Gas_Sensor.B1
  N7: Arduino.D2, alarm_buzzer.1
  N8: Light_sensor.pin_0, Tempreture_sensor.+Vs, MQ2_Gas_Sensor.A1
  N9: Tempreture_sensor.GND, alarm_buzzer.2, R2.Pin_1, MQ2_Gas_Sensor.H1
